// Logisim project 4 BIT ADDER.circ as structural Verilog: 1 circuit, main circuit main
module main (
  input  A0,
  input  B0,
  input  A1,
  input  B1,
  input  A2,
  input  B2,
  input  A3,
  input  B3,
  output S0,
  output S1,
  output S2,
  output S3,
  output S4,
  output GND
);

  wire half_adder_circuit_1_out_4, main_1_out_5, main_2_out_5, main_3_out_5;

  half_adder_circuit half_adder_circuit_1 (.in_1(A0), .in_2(B0), .out_3(S0), .out_4(half_adder_circuit_1_out_4));
  full_adder_circuit_main main_1 (
    .in_2(B1), .in_3(half_adder_circuit_1_out_4), .in_1(A1), .out_4(S1), .out_5(main_1_out_5));
  full_adder_circuit_main main_2 (.in_2(B2), .in_3(main_1_out_5), .in_1(A2), .out_4(S2), .out_5(main_2_out_5));
  full_adder_circuit_main main_3 (.in_2(B3), .in_3(main_2_out_5), .in_1(A3), .out_4(S3), .out_5(main_3_out_5));
  full_adder_circuit_main main_4 (.in_2(1'b0), .in_3(main_3_out_5), .in_1(1'b0), .out_4(S4), .out_5(GND));
endmodule
