// Logisim project 4 bit adder circuit with display.circ as structural Verilog: 1 circuit, main circuit main
module main (
  input  A0,
  input  B0,
  input  A1,
  input  B1,
  input  A2,
  input  B2,
  input  A3,
  input  B3
);

  wire bin_to_bcd_1_b0, bin_to_bcd_1_b1, bin_to_bcd_1_b2, bin_to_bcd_1_b3, bin_to_bcd_1_b4, bin_to_bcd_2_b0,
       bin_to_bcd_2_b1, bin_to_bcd_2_b2, bin_to_bcd_2_b3, bin_to_bcd_2_b4, bin_to_bcd_5i_6o_1_b0,
       bin_to_bcd_5i_6o_1_b1, bin_to_bcd_5i_6o_1_b2, bin_to_bcd_5i_6o_1_b3, bin_to_bcd_5i_6o_1_b4,
       bin_to_bcd_5i_6o_1_b5, decoder_3_1_a, decoder_3_1_b, decoder_3_1_c, decoder_3_1_d, decoder_3_1_e,
       decoder_3_1_f, decoder_3_1_g, decoder_3_2_a, decoder_3_2_b, decoder_3_2_c, decoder_3_2_d,
       decoder_3_2_e, decoder_3_2_f, decoder_3_2_g, decoder_3_3_a, decoder_3_3_b, decoder_3_3_c,
       decoder_3_3_d, decoder_3_3_e, decoder_3_3_f, decoder_3_3_g, decoder_3_4_a, decoder_3_4_b,
       decoder_3_4_c, decoder_3_4_d, decoder_3_4_e, decoder_3_4_f, decoder_3_4_g, decoder_3_5_a,
       decoder_3_5_b, decoder_3_5_c, decoder_3_5_d, decoder_3_5_e, decoder_3_5_f, decoder_3_5_g,
       decoder_3_6_a, decoder_3_6_b, decoder_3_6_c, decoder_3_6_d, decoder_3_6_e, decoder_3_6_f,
       decoder_3_6_g, main_1_gnd, main_1_s0, main_1_s1, main_1_s2, main_1_s3, main_1_s4;

  _7_Segment_Display u_7_segment_display_1 (
    .g(decoder_3_1_g), .f(decoder_3_1_f), .a(decoder_3_1_a), .b(decoder_3_1_b), .e(decoder_3_1_e),
    .d(decoder_3_1_d), .c(decoder_3_1_c), .dp(main_1_gnd));
  _7_Segment_Display u_7_segment_display_2 (
    .g(decoder_3_2_g), .f(decoder_3_2_f), .a(decoder_3_2_a), .b(decoder_3_2_b), .e(decoder_3_2_e),
    .d(decoder_3_2_d), .c(decoder_3_2_c), .dp(main_1_gnd));
  _7_Segment_Display u_7_segment_display_3 (
    .g(decoder_3_3_g), .f(decoder_3_3_f), .a(decoder_3_3_a), .b(decoder_3_3_b), .e(decoder_3_3_e),
    .d(decoder_3_3_d), .c(decoder_3_3_c), .dp(main_1_gnd));
  decoder_3 decoder_3_1 (
    .B3(main_1_gnd), .B2(main_1_gnd), .B1(main_1_gnd), .B0(bin_to_bcd_2_b4), .a(decoder_3_1_a),
    .b(decoder_3_1_b), .c(decoder_3_1_c), .d(decoder_3_1_d), .e(decoder_3_1_e), .f(decoder_3_1_f),
    .g(decoder_3_1_g));
  _7_Segment_Display u_7_segment_display_4 (
    .g(decoder_3_4_g), .f(decoder_3_4_f), .a(decoder_3_4_a), .b(decoder_3_4_b), .e(decoder_3_4_e),
    .d(decoder_3_4_d), .c(decoder_3_4_c), .dp(main_1_gnd));
  decoder_3 decoder_3_2 (
    .B3(main_1_gnd), .B2(main_1_gnd), .B1(main_1_gnd), .B0(bin_to_bcd_1_b4), .a(decoder_3_2_a),
    .b(decoder_3_2_b), .c(decoder_3_2_c), .d(decoder_3_2_d), .e(decoder_3_2_e), .f(decoder_3_2_f),
    .g(decoder_3_2_g));
  decoder_3 decoder_3_3 (
    .B3(bin_to_bcd_1_b3), .B2(bin_to_bcd_1_b2), .B1(bin_to_bcd_1_b1), .B0(bin_to_bcd_1_b0),
    .a(decoder_3_3_a), .b(decoder_3_3_b), .c(decoder_3_3_c), .d(decoder_3_3_d), .e(decoder_3_3_e),
    .f(decoder_3_3_f), .g(decoder_3_3_g));
  decoder_3 decoder_3_4 (
    .B3(bin_to_bcd_2_b3), .B2(bin_to_bcd_2_b2), .B1(bin_to_bcd_2_b1), .B0(bin_to_bcd_2_b0),
    .a(decoder_3_4_a), .b(decoder_3_4_b), .c(decoder_3_4_c), .d(decoder_3_4_d), .e(decoder_3_4_e),
    .f(decoder_3_4_f), .g(decoder_3_4_g));
  bin_to_bcd bin_to_bcd_1 (
    .A3(A3), .A2(A2), .A1(A1), .A0(A0), .B4(bin_to_bcd_1_b4), .B3(bin_to_bcd_1_b3), .B2(bin_to_bcd_1_b2),
    .B1(bin_to_bcd_1_b1), .B0(bin_to_bcd_1_b0));
  bin_to_bcd bin_to_bcd_2 (
    .A3(B3), .A2(B2), .A1(B1), .A0(B0), .B4(bin_to_bcd_2_b4), .B3(bin_to_bcd_2_b3), .B2(bin_to_bcd_2_b2),
    .B1(bin_to_bcd_2_b1), .B0(bin_to_bcd_2_b0));
  _4_BIT_ADDER_main main_1 (
    .A0(A0), .B0(B0), .A1(A1), .B1(B1), .A2(A2), .B2(B2), .A3(A3), .B3(B3), .S0(main_1_s0), .S1(main_1_s1),
    .S2(main_1_s2), .S3(main_1_s3), .S4(main_1_s4), .GND(main_1_gnd));
  BIN__TO___BCD__5I_6O bin_to_bcd_5i_6o_1 (
    .S4(main_1_s4), .S3(main_1_s3), .S2(main_1_s2), .S1(main_1_s1), .S0(main_1_s0),
    .B5(bin_to_bcd_5i_6o_1_b5), .B4(bin_to_bcd_5i_6o_1_b4), .B3(bin_to_bcd_5i_6o_1_b3),
    .B2(bin_to_bcd_5i_6o_1_b2), .B1(bin_to_bcd_5i_6o_1_b1), .B0(bin_to_bcd_5i_6o_1_b0));
  decoder_3 decoder_3_5 (
    .B3(main_1_gnd), .B2(main_1_gnd), .B1(bin_to_bcd_5i_6o_1_b5), .B0(bin_to_bcd_5i_6o_1_b4),
    .a(decoder_3_5_a), .b(decoder_3_5_b), .c(decoder_3_5_c), .d(decoder_3_5_d), .e(decoder_3_5_e),
    .f(decoder_3_5_f), .g(decoder_3_5_g));
  decoder_3 decoder_3_6 (
    .B3(bin_to_bcd_5i_6o_1_b3), .B2(bin_to_bcd_5i_6o_1_b2), .B1(bin_to_bcd_5i_6o_1_b1),
    .B0(bin_to_bcd_5i_6o_1_b0), .a(decoder_3_6_a), .b(decoder_3_6_b), .c(decoder_3_6_c), .d(decoder_3_6_d),
    .e(decoder_3_6_e), .f(decoder_3_6_f), .g(decoder_3_6_g));
  _7_Segment_Display u_7_segment_display_5 (
    .g(decoder_3_5_g), .f(decoder_3_5_f), .a(decoder_3_5_a), .b(decoder_3_5_b), .e(decoder_3_5_e),
    .d(decoder_3_5_d), .c(decoder_3_5_c), .dp(main_1_gnd));
  _7_Segment_Display u_7_segment_display_6 (
    .g(decoder_3_6_g), .f(decoder_3_6_f), .a(decoder_3_6_a), .b(decoder_3_6_b), .e(decoder_3_6_e),
    .d(decoder_3_6_d), .c(decoder_3_6_c), .dp(main_1_gnd));
  // also tied to GND on the sheet: main_1_gnd
endmodule
