// Logisim project BIN-TO-BCD 4I-50.circ as structural Verilog
module bin_to_bcd (
  input  A3,
  input  A2,
  input  A1,
  input  A0,
  output B4,
  output B3,
  output B2,
  output B1,
  output B0
);

  wire and_1_out, and_2_out, and_4_out, and_5_out, and_6_out, and_7_out, not_1_out, not_2_out, not_3_out,
       not_4_out, not_5_out;

  and and_1 (and_1_out, A3, A1);
  and and_2 (and_2_out, A3, A2);
  and and_3 (B3, A3, not_1_out, not_2_out);
  not not_1 (not_1_out, A2);
  not not_2 (not_2_out, A1);
  not not_3 (not_3_out, A3);
  and and_4 (and_4_out, not_3_out, A2);
  and and_5 (and_5_out, A2, A1);
  not not_4 (not_4_out, A3);
  and and_6 (and_6_out, not_4_out, A1);
  and and_7 (and_7_out, A3, A2, not_5_out);
  not not_5 (not_5_out, A1);
  or or_1 (B4, and_1_out, and_2_out);
  or or_2 (B2, and_4_out, and_5_out);
  or or_3 (B1, and_6_out, and_7_out);

  assign B0 = A0;
endmodule
