// Logisim project BIN-TO-BCD 5I-6O.circ as structural Verilog
module BIN__TO___BCD__5I_6O (
  input  S4,
  input  S3,
  input  S2,
  input  S1,
  input  S0,
  output B5,
  output B4,
  output B3,
  output B2,
  output B1,
  output B0
);

  wire and_1_out, and_2_out, and_3_out, and_4_out, and_5_out, and_6_out, and_7_out, and_8_out, and_9_out,
       and_10_out, and_11_out, and_12_out, and_13_out, and_14_out, and_15_out, and_16_out, and_17_out,
       and_18_out, not_1_out, not_2_out, not_3_out, not_4_out, not_5_out, not_6_out, not_7_out, not_8_out,
       not_9_out, not_10_out, not_11_out, not_12_out, not_13_out, not_14_out, not_15_out, not_16_out,
       not_17_out, not_18_out, not_19_out, not_20_out, not_21_out, not_22_out, not_23_out, not_24_out,
       not_25_out;

  and and_1 (and_1_out, S4, S2);
  and and_2 (and_2_out, S4, S3);
  not not_1 (not_1_out, S4);
  not not_2 (not_2_out, S4);
  not not_3 (not_3_out, S3);
  not not_4 (not_4_out, S2);
  not not_5 (not_5_out, S4);
  not not_6 (not_6_out, S2);
  not not_7 (not_7_out, S1);
  not not_8 (not_8_out, S3);
  not not_9 (not_9_out, S2);
  not not_10 (not_10_out, S1);
  not not_11 (not_11_out, S4);
  not not_12 (not_12_out, S3);
  not not_13 (not_13_out, S4);
  not not_14 (not_14_out, S2);
  not not_15 (not_15_out, S1);
  not not_16 (not_16_out, S2);
  not not_17 (not_17_out, S4);
  not not_18 (not_18_out, S3);
  not not_19 (not_19_out, S3);
  not not_20 (not_20_out, S4);
  not not_21 (not_21_out, S1);
  not not_22 (not_22_out, S3);
  not not_23 (not_23_out, S2);
  not not_24 (not_24_out, S1);
  not not_25 (not_25_out, S2);
  or or_1 (B5, and_1_out, and_2_out);
  and and_3 (and_3_out, not_1_out, S3, S1);
  and and_4 (and_4_out, not_2_out, S3, S2);
  and and_5 (and_5_out, S3, S2, S1);
  and and_6 (and_6_out, S4, not_3_out, not_4_out);
  and and_7 (and_7_out, not_5_out, S3, not_6_out, not_7_out);
  and and_8 (and_8_out, S4, not_8_out, not_9_out, S1);
  and and_9 (and_9_out, S4, S3, S2, not_10_out);
  and and_10 (and_10_out, not_11_out, not_12_out, S2);
  and and_11 (and_11_out, not_13_out, S2, S1);
  and and_12 (and_12_out, S4, not_14_out, not_15_out);
  and and_13 (and_13_out, S4, S3, not_16_out);
  and and_14 (and_14_out, not_17_out, not_18_out, S1);
  and and_15 (and_15_out, not_19_out, S2, S1);
  and and_16 (and_16_out, not_20_out, S3, S2, not_21_out);
  and and_17 (and_17_out, S4, not_22_out, not_23_out, not_24_out);
  and and_18 (and_18_out, S4, S3, not_25_out, S1);
  or or_2 (B4, and_3_out, and_4_out, and_5_out, and_6_out);
  or or_3 (B3, and_7_out, and_8_out, and_9_out);
  or or_4 (B2, and_10_out, and_11_out, and_12_out, and_13_out);
  or or_5 (B1, and_14_out, and_15_out, and_16_out, and_17_out, and_18_out);

  assign B0 = S0;
endmodule
