// Logisim project DECODER 4I-8O.circ as structural Verilog
module decoder_3 (
  input  B3,
  input  B2,
  input  B1,
  input  B0,
  output a,
  output b,
  output c,
  output d,
  output e,
  output f,
  output g
);

  wire and_1_out, and_2_out, and_3_out, and_4_out, and_5_out, and_6_out, and_7_out, and_8_out, and_9_out,
       and_10_out, and_11_out, and_12_out, and_13_out, not_1_out, not_2_out, not_3_out, not_4_out, not_5_out,
       not_6_out, not_7_out, not_8_out, not_9_out, not_10_out, not_11_out, not_12_out, not_13_out,
       not_14_out, not_15_out, not_16_out, not_17_out, not_18_out;

  not not_1 (not_1_out, B2);
  and and_1 (and_1_out, not_1_out, not_2_out);
  not not_2 (not_2_out, B0);
  and and_2 (and_2_out, B2, B0);
  not not_3 (not_3_out, B2);
  not not_4 (not_4_out, B1);
  and and_3 (and_3_out, not_4_out, not_5_out);
  not not_5 (not_5_out, B0);
  and and_4 (and_4_out, B1, B0);
  not not_6 (not_6_out, B1);
  or or_1 (c, not_6_out, B0, B2);
  not not_7 (not_7_out, B2);
  and and_5 (and_5_out, not_7_out, not_8_out);
  not not_8 (not_8_out, B0);
  not not_9 (not_9_out, B2);
  and and_6 (and_6_out, not_9_out, B1);
  and and_7 (and_7_out, B1, not_10_out);
  not not_10 (not_10_out, B0);
  and and_8 (and_8_out, B2, not_11_out, B0);
  not not_11 (not_11_out, B1);
  not not_12 (not_12_out, B2);
  and and_9 (and_9_out, not_12_out, not_13_out);
  not not_13 (not_13_out, B0);
  and and_10 (and_10_out, B1, not_14_out);
  not not_14 (not_14_out, B0);
  not not_15 (not_15_out, B1);
  and and_11 (and_11_out, not_15_out, not_16_out);
  not not_16 (not_16_out, B0);
  and and_12 (and_12_out, B2, not_17_out);
  not not_17 (not_17_out, B1);
  and and_13 (and_13_out, B2, not_18_out);
  not not_18 (not_18_out, B0);
  or or_2 (g, B1, B2, B3);
  or or_3 (a, and_1_out, B1, and_2_out, B3);
  or or_4 (b, not_3_out, and_3_out, and_4_out);
  or or_5 (d, and_5_out, and_6_out, and_7_out, and_8_out, B3);
  or or_6 (e, and_9_out, and_10_out);
  or or_7 (f, and_11_out, and_12_out, and_13_out, B3);
endmodule
