// Logisim project full adder circuit.circ as structural Verilog: 2 circuits, main circuit main
module main (
  input  in_1,
  input  in_2,
  input  in_3,
  output out_4,
  output out_5
);

  wire and_1_out, and_2_out, xor_1_out;

  xor xor_1 (xor_1_out, in_1, in_2);
  and and_1 (and_1_out, in_1, in_2);
  xor xor_2 (out_4, xor_1_out, in_3);
  and and_2 (and_2_out, xor_1_out, in_3);
  or or_1 (out_5, and_2_out, and_1_out);
endmodule

module full_adder_circuit (
);

  wire undriven, undriven_2;
  wire [3:0] bitadder_1_out;
  wire [7:0] undriven_3;

  main main_1 (.in_3(undriven_2), .in_1(undriven));  // open: in_2, out_4, out_5
  BitAdder bitadder_1 (.in0(undriven_3), .out(bitadder_1_out));
endmodule
